// Logisim project 사현진 logisim 파일.circ as structural Verilog: 1 circuit, main circuit main
module main (
  input  y,
  input  a,
  input  b,
  input  x,
  input  x_2,
  input  c,
  input  y_2,
  input  d,
  input  a_2,
  input  b_2,
  input  c_2,
  output F1,
  output F2,
  output F3
);

  wire and_1_out, and_2_out, and_3_out, and_4_out, and_5_out, and_6_out, and_7_out, and_8_out, not_1_out,
       not_2_out, not_3_out, not_4_out, not_5_out, not_6_out, xor_1_out;

  not not_1 (not_1_out, x_2);
  not not_2 (not_2_out, y);
  and and_1 (and_1_out, y, not_1_out);
  and and_2 (and_2_out, not_2_out, x_2);
  and and_3 (and_3_out, a_2, b_2);
  xor xor_1 (xor_1_out, a_2, b_2);
  or or_1 (F1, and_1_out, and_2_out);
  and and_4 (and_4_out, xor_1_out, c_2);
  or or_2 (F3, and_3_out, and_4_out);
  not not_3 (not_3_out, x);
  not not_4 (not_4_out, y_2);
  not not_5 (not_5_out, y_2);
  not not_6 (not_6_out, x);
  and and_5 (and_5_out, a, not_3_out, not_4_out);
  and and_6 (and_6_out, b, x, not_5_out);
  and and_7 (and_7_out, c, not_6_out, y_2);
  and and_8 (and_8_out, d, x, y_2);
  or or_3 (F2, and_5_out, and_6_out, and_7_out, and_8_out);
endmodule
